// Logisim project Simulation.circ as structural Verilog
module Sign_Calculator (
  input  [7:0] Multiplier,
  input  [7:0] Multiplicand,
  output [7:0] ABS_Multiplier,
  output Sign,
  output [7:0] ABS_Multiplicand
);

  wire [6:0] xor_2_out, xor_4_out;

  xor xor_1 (xor_2_out[1], Multiplier[1], Multiplier[7]);
  xor xor_2 (xor_2_out[0], Multiplier[0], Multiplier[7]);
  xor xor_3 (xor_4_out[1], Multiplicand[1], Multiplicand[7]);
  xor xor_4 (xor_4_out[0], Multiplicand[0], Multiplicand[7]);
  xor xor_5 (xor_2_out[2], Multiplier[2], Multiplier[7]);
  xor xor_6 (xor_4_out[2], Multiplicand[2], Multiplicand[7]);
  xor xor_7 (xor_2_out[4], Multiplier[4], Multiplier[7]);
  xor xor_8 (xor_2_out[3], Multiplier[3], Multiplier[7]);
  xor xor_9 (xor_4_out[4], Multiplicand[4], Multiplicand[7]);
  xor xor_10 (xor_4_out[3], Multiplicand[3], Multiplicand[7]);
  xor xor_11 (xor_2_out[6], Multiplier[6], Multiplier[7]);
  xor xor_12 (xor_2_out[5], Multiplier[5], Multiplier[7]);
  Adder adder_1 (.a({8{1'b0}}), .b({1'b0, xor_2_out}), .out(ABS_Multiplier), .cin(Multiplier[7]));  // open: cout
  xor xor_13 (xor_4_out[6], Multiplicand[6], Multiplicand[7]);
  xor xor_14 (xor_4_out[5], Multiplicand[5], Multiplicand[7]);
  Adder adder_2 (.a({8{1'b0}}), .b({1'b0, xor_4_out}), .out(ABS_Multiplicand), .cin(Multiplicand[7]));  // open: cout
  xor xor_15 (Sign, Multiplier[7], Multiplicand[7]);
endmodule

module Binary_to_BCD (
  input  [15:0] Binary_IN,
  output [3:0] D4,
  output [3:0] D3,
  output [3:0] D2,
  output [3:0] D1,
  output [3:0] D0
);

  wire add_3_if_ge_5_4_out0, add_3_if_ge_5_4_out1, add_3_if_ge_5_4_out2, add_3_if_ge_5_4_out3,
       add_3_if_ge_5_5_out0, add_3_if_ge_5_5_out1, add_3_if_ge_5_5_out2, add_3_if_ge_5_5_out3,
       add_3_if_ge_5_6_out0, add_3_if_ge_5_6_out1, add_3_if_ge_5_6_out2, add_3_if_ge_5_6_out3,
       add_3_if_ge_5_7_out0, add_3_if_ge_5_7_out1, add_3_if_ge_5_7_out2, add_3_if_ge_5_7_out3,
       add_3_if_ge_5_8_out0, add_3_if_ge_5_8_out1, add_3_if_ge_5_8_out2, add_3_if_ge_5_8_out3,
       add_3_if_ge_5_9_out0, add_3_if_ge_5_9_out1, add_3_if_ge_5_9_out2, add_3_if_ge_5_9_out3,
       add_3_if_ge_5_10_out0, add_3_if_ge_5_10_out1, add_3_if_ge_5_10_out2, add_3_if_ge_5_10_out3,
       add_3_if_ge_5_11_out0, add_3_if_ge_5_11_out1, add_3_if_ge_5_11_out2, add_3_if_ge_5_11_out3,
       add_3_if_ge_5_12_out0, add_3_if_ge_5_12_out1, add_3_if_ge_5_12_out2, add_3_if_ge_5_12_out3,
       add_3_if_ge_5_13_out0, add_3_if_ge_5_13_out1, add_3_if_ge_5_13_out2, add_3_if_ge_5_13_out3,
       add_3_if_ge_5_14_out0, add_3_if_ge_5_14_out1, add_3_if_ge_5_14_out2, add_3_if_ge_5_14_out3,
       add_3_if_ge_5_15_out0, add_3_if_ge_5_15_out1, add_3_if_ge_5_15_out2, add_3_if_ge_5_15_out3,
       add_3_if_ge_5_16_out0, add_3_if_ge_5_16_out1, add_3_if_ge_5_16_out2, add_3_if_ge_5_16_out3,
       add_3_if_ge_5_17_out0, add_3_if_ge_5_17_out1, add_3_if_ge_5_17_out2, add_3_if_ge_5_17_out3,
       add_3_if_ge_5_18_out0, add_3_if_ge_5_18_out1, add_3_if_ge_5_18_out2, add_3_if_ge_5_18_out3,
       add_3_if_ge_5_19_out0, add_3_if_ge_5_19_out1, add_3_if_ge_5_19_out2, add_3_if_ge_5_19_out3,
       add_3_if_ge_5_20_out0, add_3_if_ge_5_20_out1, add_3_if_ge_5_20_out2, add_3_if_ge_5_20_out3,
       add_3_if_ge_5_21_out0, add_3_if_ge_5_21_out1, add_3_if_ge_5_21_out2, add_3_if_ge_5_21_out3,
       add_3_if_ge_5_22_out0, add_3_if_ge_5_22_out1, add_3_if_ge_5_22_out2, add_3_if_ge_5_22_out3,
       add_3_if_ge_5_23_out0, add_3_if_ge_5_23_out1, add_3_if_ge_5_23_out2, add_3_if_ge_5_23_out3,
       add_3_if_ge_5_26_out0, add_3_if_ge_5_26_out1, add_3_if_ge_5_26_out2, add_3_if_ge_5_26_out3,
       add_3_if_ge_5_27_out0, add_3_if_ge_5_27_out1, add_3_if_ge_5_27_out2, add_3_if_ge_5_27_out3,
       add_3_if_ge_5_28_out0, add_3_if_ge_5_28_out1, add_3_if_ge_5_28_out2, add_3_if_ge_5_28_out3,
       add_3_if_ge_5_29_out0, add_3_if_ge_5_29_out1, add_3_if_ge_5_29_out2, add_3_if_ge_5_29_out3,
       add_3_if_ge_5_30_out0, add_3_if_ge_5_30_out1, add_3_if_ge_5_30_out2, add_3_if_ge_5_30_out3,
       add_3_if_ge_5_31_out0, add_3_if_ge_5_31_out1, add_3_if_ge_5_31_out2, add_3_if_ge_5_31_out3,
       add_3_if_ge_5_32_out0, add_3_if_ge_5_32_out1, add_3_if_ge_5_32_out2, add_3_if_ge_5_32_out3,
       add_3_if_ge_5_33_out0, add_3_if_ge_5_33_out1, add_3_if_ge_5_33_out2, add_3_if_ge_5_33_out3,
       add_3_if_ge_5_34_out0, add_3_if_ge_5_34_out1, add_3_if_ge_5_34_out2, add_3_if_ge_5_34_out3,
       add_3_if_ge_5_35_out0, add_3_if_ge_5_35_out1, add_3_if_ge_5_35_out2, add_3_if_ge_5_35_out3;

  Add_3_if_GE_5 add_3_if_ge_5_1 (
    .IN3(1'b0), .IN2(add_3_if_ge_5_9_out3), .IN1(add_3_if_ge_5_7_out3), .IN0(add_3_if_ge_5_4_out3),
    .OUT2(D4[3]), .OUT1(D4[2]), .OUT0(D4[1]));  // open: OUT3
  Add_3_if_GE_5 add_3_if_ge_5_2 (
    .IN3(add_3_if_ge_5_4_out2), .IN2(add_3_if_ge_5_4_out1), .IN1(add_3_if_ge_5_4_out0),
    .IN0(add_3_if_ge_5_5_out3), .OUT3(D4[0]), .OUT2(D3[3]), .OUT1(D3[2]), .OUT0(D3[1]));
  Add_3_if_GE_5 add_3_if_ge_5_3 (
    .IN3(add_3_if_ge_5_5_out2), .IN2(add_3_if_ge_5_5_out1), .IN1(add_3_if_ge_5_5_out0),
    .IN0(add_3_if_ge_5_26_out3), .OUT3(D3[0]), .OUT2(D2[3]), .OUT1(D2[2]), .OUT0(D2[1]));
  Add_3_if_GE_5 add_3_if_ge_5_4 (
    .IN3(add_3_if_ge_5_7_out2), .IN2(add_3_if_ge_5_7_out1), .IN1(add_3_if_ge_5_7_out0),
    .IN0(add_3_if_ge_5_6_out3), .OUT3(add_3_if_ge_5_4_out3), .OUT2(add_3_if_ge_5_4_out2),
    .OUT1(add_3_if_ge_5_4_out1), .OUT0(add_3_if_ge_5_4_out0));
  Add_3_if_GE_5 add_3_if_ge_5_5 (
    .IN3(add_3_if_ge_5_6_out2), .IN2(add_3_if_ge_5_6_out1), .IN1(add_3_if_ge_5_6_out0),
    .IN0(add_3_if_ge_5_28_out3), .OUT3(add_3_if_ge_5_5_out3), .OUT2(add_3_if_ge_5_5_out2),
    .OUT1(add_3_if_ge_5_5_out1), .OUT0(add_3_if_ge_5_5_out0));
  Add_3_if_GE_5 add_3_if_ge_5_6 (
    .IN3(add_3_if_ge_5_8_out2), .IN2(add_3_if_ge_5_8_out1), .IN1(add_3_if_ge_5_8_out0),
    .IN0(add_3_if_ge_5_30_out3), .OUT3(add_3_if_ge_5_6_out3), .OUT2(add_3_if_ge_5_6_out2),
    .OUT1(add_3_if_ge_5_6_out1), .OUT0(add_3_if_ge_5_6_out0));
  Add_3_if_GE_5 add_3_if_ge_5_7 (
    .IN3(add_3_if_ge_5_9_out2), .IN2(add_3_if_ge_5_9_out1), .IN1(add_3_if_ge_5_9_out0),
    .IN0(add_3_if_ge_5_8_out3), .OUT3(add_3_if_ge_5_7_out3), .OUT2(add_3_if_ge_5_7_out2),
    .OUT1(add_3_if_ge_5_7_out1), .OUT0(add_3_if_ge_5_7_out0));
  Add_3_if_GE_5 add_3_if_ge_5_8 (
    .IN3(add_3_if_ge_5_10_out2), .IN2(add_3_if_ge_5_10_out1), .IN1(add_3_if_ge_5_10_out0),
    .IN0(add_3_if_ge_5_11_out3), .OUT3(add_3_if_ge_5_8_out3), .OUT2(add_3_if_ge_5_8_out2),
    .OUT1(add_3_if_ge_5_8_out1), .OUT0(add_3_if_ge_5_8_out0));
  Add_3_if_GE_5 add_3_if_ge_5_9 (
    .IN3(1'b0), .IN2(add_3_if_ge_5_15_out3), .IN1(add_3_if_ge_5_12_out3), .IN0(add_3_if_ge_5_10_out3),
    .OUT3(add_3_if_ge_5_9_out3), .OUT2(add_3_if_ge_5_9_out2), .OUT1(add_3_if_ge_5_9_out1),
    .OUT0(add_3_if_ge_5_9_out0));
  Add_3_if_GE_5 add_3_if_ge_5_10 (
    .IN3(add_3_if_ge_5_12_out2), .IN2(add_3_if_ge_5_12_out1), .IN1(add_3_if_ge_5_12_out0),
    .IN0(add_3_if_ge_5_13_out3), .OUT3(add_3_if_ge_5_10_out3), .OUT2(add_3_if_ge_5_10_out2),
    .OUT1(add_3_if_ge_5_10_out1), .OUT0(add_3_if_ge_5_10_out0));
  Add_3_if_GE_5 add_3_if_ge_5_11 (
    .IN3(add_3_if_ge_5_13_out2), .IN2(add_3_if_ge_5_13_out1), .IN1(add_3_if_ge_5_13_out0),
    .IN0(add_3_if_ge_5_33_out3), .OUT3(add_3_if_ge_5_11_out3), .OUT2(add_3_if_ge_5_11_out2),
    .OUT1(add_3_if_ge_5_11_out1), .OUT0(add_3_if_ge_5_11_out0));
  Add_3_if_GE_5 add_3_if_ge_5_12 (
    .IN3(add_3_if_ge_5_15_out2), .IN2(add_3_if_ge_5_15_out1), .IN1(add_3_if_ge_5_15_out0),
    .IN0(add_3_if_ge_5_14_out3), .OUT3(add_3_if_ge_5_12_out3), .OUT2(add_3_if_ge_5_12_out2),
    .OUT1(add_3_if_ge_5_12_out1), .OUT0(add_3_if_ge_5_12_out0));
  Add_3_if_GE_5 add_3_if_ge_5_13 (
    .IN3(add_3_if_ge_5_14_out2), .IN2(add_3_if_ge_5_14_out1), .IN1(add_3_if_ge_5_14_out0),
    .IN0(add_3_if_ge_5_34_out3), .OUT3(add_3_if_ge_5_13_out3), .OUT2(add_3_if_ge_5_13_out2),
    .OUT1(add_3_if_ge_5_13_out1), .OUT0(add_3_if_ge_5_13_out0));
  Add_3_if_GE_5 add_3_if_ge_5_14 (
    .IN3(add_3_if_ge_5_16_out2), .IN2(add_3_if_ge_5_16_out1), .IN1(add_3_if_ge_5_16_out0),
    .IN0(add_3_if_ge_5_35_out3), .OUT3(add_3_if_ge_5_14_out3), .OUT2(add_3_if_ge_5_14_out2),
    .OUT1(add_3_if_ge_5_14_out1), .OUT0(add_3_if_ge_5_14_out0));
  Add_3_if_GE_5 add_3_if_ge_5_15 (
    .IN3(1'b0), .IN2(add_3_if_ge_5_19_out3), .IN1(add_3_if_ge_5_17_out3), .IN0(add_3_if_ge_5_16_out3),
    .OUT3(add_3_if_ge_5_15_out3), .OUT2(add_3_if_ge_5_15_out2), .OUT1(add_3_if_ge_5_15_out1),
    .OUT0(add_3_if_ge_5_15_out0));
  Add_3_if_GE_5 add_3_if_ge_5_16 (
    .IN3(add_3_if_ge_5_17_out2), .IN2(add_3_if_ge_5_17_out1), .IN1(add_3_if_ge_5_17_out0),
    .IN0(add_3_if_ge_5_18_out3), .OUT3(add_3_if_ge_5_16_out3), .OUT2(add_3_if_ge_5_16_out2),
    .OUT1(add_3_if_ge_5_16_out1), .OUT0(add_3_if_ge_5_16_out0));
  Add_3_if_GE_5 add_3_if_ge_5_17 (
    .IN3(add_3_if_ge_5_19_out2), .IN2(add_3_if_ge_5_19_out1), .IN1(add_3_if_ge_5_19_out0),
    .IN0(add_3_if_ge_5_20_out3), .OUT3(add_3_if_ge_5_17_out3), .OUT2(add_3_if_ge_5_17_out2),
    .OUT1(add_3_if_ge_5_17_out1), .OUT0(add_3_if_ge_5_17_out0));
  Add_3_if_GE_5 add_3_if_ge_5_18 (
    .IN3(add_3_if_ge_5_20_out2), .IN2(add_3_if_ge_5_20_out1), .IN1(add_3_if_ge_5_20_out0),
    .IN0(Binary_IN[9]), .OUT3(add_3_if_ge_5_18_out3), .OUT2(add_3_if_ge_5_18_out2),
    .OUT1(add_3_if_ge_5_18_out1), .OUT0(add_3_if_ge_5_18_out0));
  Add_3_if_GE_5 add_3_if_ge_5_19 (
    .IN3(1'b0), .IN2(add_3_if_ge_5_23_out3), .IN1(add_3_if_ge_5_22_out3), .IN0(add_3_if_ge_5_21_out3),
    .OUT3(add_3_if_ge_5_19_out3), .OUT2(add_3_if_ge_5_19_out2), .OUT1(add_3_if_ge_5_19_out1),
    .OUT0(add_3_if_ge_5_19_out0));
  Add_3_if_GE_5 add_3_if_ge_5_20 (
    .IN3(add_3_if_ge_5_21_out2), .IN2(add_3_if_ge_5_21_out1), .IN1(add_3_if_ge_5_21_out0),
    .IN0(Binary_IN[10]), .OUT3(add_3_if_ge_5_20_out3), .OUT2(add_3_if_ge_5_20_out2),
    .OUT1(add_3_if_ge_5_20_out1), .OUT0(add_3_if_ge_5_20_out0));
  Add_3_if_GE_5 add_3_if_ge_5_21 (
    .IN3(add_3_if_ge_5_22_out2), .IN2(add_3_if_ge_5_22_out1), .IN1(add_3_if_ge_5_22_out0),
    .IN0(Binary_IN[11]), .OUT3(add_3_if_ge_5_21_out3), .OUT2(add_3_if_ge_5_21_out2),
    .OUT1(add_3_if_ge_5_21_out1), .OUT0(add_3_if_ge_5_21_out0));
  Add_3_if_GE_5 add_3_if_ge_5_22 (
    .IN3(add_3_if_ge_5_23_out2), .IN2(add_3_if_ge_5_23_out1), .IN1(add_3_if_ge_5_23_out0),
    .IN0(Binary_IN[12]), .OUT3(add_3_if_ge_5_22_out3), .OUT2(add_3_if_ge_5_22_out2),
    .OUT1(add_3_if_ge_5_22_out1), .OUT0(add_3_if_ge_5_22_out0));
  Add_3_if_GE_5 add_3_if_ge_5_23 (
    .IN3(1'b0), .IN2(Binary_IN[15]), .IN1(Binary_IN[14]), .IN0(Binary_IN[13]), .OUT3(add_3_if_ge_5_23_out3),
    .OUT2(add_3_if_ge_5_23_out2), .OUT1(add_3_if_ge_5_23_out1), .OUT0(add_3_if_ge_5_23_out0));
  Add_3_if_GE_5 add_3_if_ge_5_24 (
    .IN3(add_3_if_ge_5_26_out2), .IN2(add_3_if_ge_5_26_out1), .IN1(add_3_if_ge_5_26_out0),
    .IN0(add_3_if_ge_5_27_out3), .OUT3(D2[0]), .OUT2(D1[3]), .OUT1(D1[2]), .OUT0(D1[1]));
  Add_3_if_GE_5 add_3_if_ge_5_25 (
    .IN3(add_3_if_ge_5_27_out2), .IN2(add_3_if_ge_5_27_out1), .IN1(add_3_if_ge_5_27_out0),
    .IN0(Binary_IN[1]), .OUT3(D1[0]), .OUT2(D0[3]), .OUT1(D0[2]), .OUT0(D0[1]));
  Add_3_if_GE_5 add_3_if_ge_5_26 (
    .IN3(add_3_if_ge_5_28_out2), .IN2(add_3_if_ge_5_28_out1), .IN1(add_3_if_ge_5_28_out0),
    .IN0(add_3_if_ge_5_29_out3), .OUT3(add_3_if_ge_5_26_out3), .OUT2(add_3_if_ge_5_26_out2),
    .OUT1(add_3_if_ge_5_26_out1), .OUT0(add_3_if_ge_5_26_out0));
  Add_3_if_GE_5 add_3_if_ge_5_27 (
    .IN3(add_3_if_ge_5_29_out2), .IN2(add_3_if_ge_5_29_out1), .IN1(add_3_if_ge_5_29_out0),
    .IN0(Binary_IN[2]), .OUT3(add_3_if_ge_5_27_out3), .OUT2(add_3_if_ge_5_27_out2),
    .OUT1(add_3_if_ge_5_27_out1), .OUT0(add_3_if_ge_5_27_out0));
  Add_3_if_GE_5 add_3_if_ge_5_28 (
    .IN3(add_3_if_ge_5_30_out2), .IN2(add_3_if_ge_5_30_out1), .IN1(add_3_if_ge_5_30_out0),
    .IN0(add_3_if_ge_5_31_out3), .OUT3(add_3_if_ge_5_28_out3), .OUT2(add_3_if_ge_5_28_out2),
    .OUT1(add_3_if_ge_5_28_out1), .OUT0(add_3_if_ge_5_28_out0));
  Add_3_if_GE_5 add_3_if_ge_5_29 (
    .IN3(add_3_if_ge_5_31_out2), .IN2(add_3_if_ge_5_31_out1), .IN1(add_3_if_ge_5_31_out0),
    .IN0(Binary_IN[3]), .OUT3(add_3_if_ge_5_29_out3), .OUT2(add_3_if_ge_5_29_out2),
    .OUT1(add_3_if_ge_5_29_out1), .OUT0(add_3_if_ge_5_29_out0));
  Add_3_if_GE_5 add_3_if_ge_5_30 (
    .IN3(add_3_if_ge_5_11_out2), .IN2(add_3_if_ge_5_11_out1), .IN1(add_3_if_ge_5_11_out0),
    .IN0(add_3_if_ge_5_32_out3), .OUT3(add_3_if_ge_5_30_out3), .OUT2(add_3_if_ge_5_30_out2),
    .OUT1(add_3_if_ge_5_30_out1), .OUT0(add_3_if_ge_5_30_out0));
  Add_3_if_GE_5 add_3_if_ge_5_31 (
    .IN3(add_3_if_ge_5_32_out2), .IN2(add_3_if_ge_5_32_out1), .IN1(add_3_if_ge_5_32_out0),
    .IN0(Binary_IN[4]), .OUT3(add_3_if_ge_5_31_out3), .OUT2(add_3_if_ge_5_31_out2),
    .OUT1(add_3_if_ge_5_31_out1), .OUT0(add_3_if_ge_5_31_out0));
  Add_3_if_GE_5 add_3_if_ge_5_32 (
    .IN3(add_3_if_ge_5_33_out2), .IN2(add_3_if_ge_5_33_out1), .IN1(add_3_if_ge_5_33_out0),
    .IN0(Binary_IN[5]), .OUT3(add_3_if_ge_5_32_out3), .OUT2(add_3_if_ge_5_32_out2),
    .OUT1(add_3_if_ge_5_32_out1), .OUT0(add_3_if_ge_5_32_out0));
  Add_3_if_GE_5 add_3_if_ge_5_33 (
    .IN3(add_3_if_ge_5_34_out2), .IN2(add_3_if_ge_5_34_out1), .IN1(add_3_if_ge_5_34_out0),
    .IN0(Binary_IN[6]), .OUT3(add_3_if_ge_5_33_out3), .OUT2(add_3_if_ge_5_33_out2),
    .OUT1(add_3_if_ge_5_33_out1), .OUT0(add_3_if_ge_5_33_out0));
  Add_3_if_GE_5 add_3_if_ge_5_34 (
    .IN3(add_3_if_ge_5_35_out2), .IN2(add_3_if_ge_5_35_out1), .IN1(add_3_if_ge_5_35_out0),
    .IN0(Binary_IN[7]), .OUT3(add_3_if_ge_5_34_out3), .OUT2(add_3_if_ge_5_34_out2),
    .OUT1(add_3_if_ge_5_34_out1), .OUT0(add_3_if_ge_5_34_out0));
  Add_3_if_GE_5 add_3_if_ge_5_35 (
    .IN3(add_3_if_ge_5_18_out2), .IN2(add_3_if_ge_5_18_out1), .IN1(add_3_if_ge_5_18_out0),
    .IN0(Binary_IN[8]), .OUT3(add_3_if_ge_5_35_out3), .OUT2(add_3_if_ge_5_35_out2),
    .OUT1(add_3_if_ge_5_35_out1), .OUT0(add_3_if_ge_5_35_out0));

  assign D0[0] = Binary_IN[0];
endmodule

module Add_3_if_GE_5 (
  input  IN3,
  input  IN2,
  input  IN1,
  input  IN0,
  output OUT3,
  output OUT2,
  output OUT1,
  output OUT0
);

  wire and_1_out, and_2_out, or_1_out;
  wire [3:0] adder_1_out;

  and and_1 (and_1_out, IN1, IN2);
  and and_2 (and_2_out, IN0, IN2);
  Adder #(.width(4)) adder_1 (.a({IN3, IN2, IN1, IN0}), .b(4'b0011), .out(adder_1_out), .cin(1'b0));  // open: cout
  Multiplexer #(.width(4)) multiplexer_1 (
    .in0({IN3, IN2, IN1, IN0}), .in1(adder_1_out), .out({OUT3, OUT2, OUT1, OUT0}), .sel(or_1_out));
  or or_1 (or_1_out, and_1_out, and_2_out, IN3);
endmodule
